// Logisim project templeOS2.circ as structural Verilog
module bit_memory (
  input  in_1,
  input  in_2,
  input  in_3,
  output out_4
);

  wire and_1_out, not_1_out, not_2_out, or_2_out;

  and and_1 (and_1_out, in_3, in_1);
  not not_1 (not_1_out, or_2_out);
  not not_2 (not_2_out, out_4);
  or or_1 (out_4, and_1_out, not_1_out);
  or or_2 (or_2_out, in_2, not_2_out);
endmodule

module _8_bit_memory (
  input  [7:0] in_1,
  input  store,
  input  reset,
  output [7:0] out_4
);

  bit_memory bit_memory_1 (.in_1(in_1[0]), .in_2(reset), .in_3(store), .out_4(out_4[0]));
  bit_memory bit_memory_2 (.in_1(in_1[1]), .in_2(reset), .in_3(store), .out_4(out_4[1]));
  bit_memory bit_memory_3 (.in_1(in_1[2]), .in_2(reset), .in_3(store), .out_4(out_4[2]));
  bit_memory bit_memory_4 (.in_1(in_1[3]), .in_2(reset), .in_3(store), .out_4(out_4[3]));
  bit_memory bit_memory_5 (.in_1(in_1[4]), .in_2(reset), .in_3(store), .out_4(out_4[4]));
  bit_memory bit_memory_6 (.in_1(in_1[5]), .in_2(reset), .in_3(store), .out_4(out_4[5]));
  bit_memory bit_memory_7 (.in_1(in_1[6]), .in_2(reset), .in_3(store), .out_4(out_4[6]));
  bit_memory bit_memory_8 (.in_1(in_1[7]), .in_2(reset), .in_3(store), .out_4(out_4[7]));
endmodule
