// Logisim project testing.circ as structural Verilog: 7 circuits, main circuit main
module main (
  input  [3:0] in_1,
  input  [15:0] in_2,
  input  [15:0] in_3,
  output [15:0] out_4,
  output out_5
);

  wire _1_out;
  wire [6:0] base10_to_display_1_out_2;
  wire [9:0] n4_bit_to_base10_1_out_2;

  Button _1 (.out(_1_out));
  _7_Segment_Display u_7_segment_display_1 (.e(_1_out), .dp(_1_out));  // open: g, f, a, b, d, c
  _16_bit_addition u_16_bit_addition_1 (
    .in_2(in_2[15]), .in_3(in_2[14]), .in_5(in_2[13]), .in_6(in_2[12]), .in_13(in_2[11]), .in_15(in_2[10]),
    .in_16(in_2[9]), .in_18(in_2[8]), .in_21(in_2[7]), .in_23(in_2[6]), .in_24(in_2[5]), .in_26(in_2[4]),
    .in_29(in_2[3]), .in_30(in_2[2]), .in_31(in_2[1]), .in_32(in_2[0]), .out_34(out_5), .out_35(out_4[15]),
    .out_36(out_4[14]), .out_37(out_4[13]), .out_38(out_4[12]), .out_39(out_4[11]), .out_40(out_4[10]),
    .out_41(out_4[9]), .out_42(out_4[8]), .out_43(out_4[7]), .out_44(out_4[6]), .out_45(out_4[5]),
    .out_46(out_4[4]), .out_47(out_4[3]), .out_48(out_4[2]), .out_49(out_4[1]), .out_50(out_4[0]),
    .in_33(1'b0), .in_1(in_3[15]), .in_4(in_3[14]), .in_7(in_3[13]), .in_8(in_3[12]), .in_9(in_3[11]),
    .in_10(in_3[10]), .in_11(in_3[9]), .in_12(in_3[8]), .in_14(in_3[7]), .in_17(in_3[6]), .in_19(in_3[5]),
    .in_20(in_3[4]), .in_22(in_3[3]), .in_25(in_3[2]), .in_27(in_3[1]), .in_28(in_3[0]));
  _4_bit_to_base10 u_4_bit_to_base10_1 (.in_1(in_1), .out_2(n4_bit_to_base10_1_out_2));
  base10_to_display base10_to_display_1 (.in_1(n4_bit_to_base10_1_out_2), .out_2(base10_to_display_1_out_2));
  _7_Segment_Display u_7_segment_display_2 (
    .g(base10_to_display_1_out_2[3]), .f(base10_to_display_1_out_2[2]), .a(base10_to_display_1_out_2[1]),
    .b(base10_to_display_1_out_2[0]), .e(base10_to_display_1_out_2[4]), .d(base10_to_display_1_out_2[5]),
    .c(base10_to_display_1_out_2[6]));  // open: dp
endmodule

module _1_bit_sum (
  input  in_1,
  input  in_2,
  input  in_3,
  output out_4,
  output out_5
);

  wire and_1_out, and_2_out, and_3_out, and_4_out, and_5_out, not_1_out, or_1_out;

  and and_1 (and_1_out, in_1, in_2);
  and and_2 (and_2_out, in_1, in_3);
  and and_3 (and_3_out, in_2, in_3);
  not not_1 (not_1_out, out_4);
  or or_1 (or_1_out, in_1, in_2, in_3);
  or or_2 (out_4, and_1_out, and_2_out, and_3_out);
  and and_4 (and_4_out, and_2_out, and_3_out);
  and and_5 (and_5_out, not_1_out, or_1_out);
  or or_3 (out_5, and_4_out, and_5_out);
endmodule

module _4_bit_sum (
  input  in_1,
  input  in_2,
  input  in_3,
  input  in_4,
  input  in_5,
  input  in_6,
  input  in_7,
  input  in_8,
  input  in_9,
  output out_10,
  output out_11,
  output out_12,
  output out_13,
  output out_14
);

  wire n1_bit_sum_2_out_4, n1_bit_sum_3_out_4, n1_bit_sum_4_out_4;

  _1_bit_sum u_1_bit_sum_1 (.in_1(in_1), .in_2(in_5), .out_4(out_10), .in_3(n1_bit_sum_2_out_4), .out_5(out_11));
  _1_bit_sum u_1_bit_sum_2 (
    .in_1(in_2), .in_2(in_6), .out_4(n1_bit_sum_2_out_4), .in_3(n1_bit_sum_3_out_4), .out_5(out_12));
  _1_bit_sum u_1_bit_sum_3 (
    .in_1(in_3), .in_2(in_7), .out_4(n1_bit_sum_3_out_4), .in_3(n1_bit_sum_4_out_4), .out_5(out_13));
  _1_bit_sum u_1_bit_sum_4 (.in_1(in_4), .in_2(in_8), .out_4(n1_bit_sum_4_out_4), .in_3(in_9), .out_5(out_14));
endmodule

module _16_bit_addition (
  input  in_1,
  input  in_2,
  input  in_3,
  input  in_4,
  input  in_5,
  input  in_6,
  input  in_7,
  input  in_8,
  input  in_9,
  input  in_10,
  input  in_11,
  input  in_12,
  input  in_13,
  input  in_14,
  input  in_15,
  input  in_16,
  input  in_17,
  input  in_18,
  input  in_19,
  input  in_20,
  input  in_21,
  input  in_22,
  input  in_23,
  input  in_24,
  input  in_25,
  input  in_26,
  input  in_27,
  input  in_28,
  input  in_29,
  input  in_30,
  input  in_31,
  input  in_32,
  input  in_33,
  output out_34,
  output out_35,
  output out_36,
  output out_37,
  output out_38,
  output out_39,
  output out_40,
  output out_41,
  output out_42,
  output out_43,
  output out_44,
  output out_45,
  output out_46,
  output out_47,
  output out_48,
  output out_49,
  output out_50
);

  wire n4_bit_sum_2_out_10, n4_bit_sum_3_out_10, n4_bit_sum_4_out_10;

  _4_bit_sum u_4_bit_sum_1 (
    .in_1(in_1), .in_2(in_4), .in_3(in_7), .in_4(in_8), .in_5(in_2), .in_6(in_3), .in_7(in_5), .in_8(in_6),
    .out_10(out_34), .in_9(n4_bit_sum_2_out_10), .out_11(out_35), .out_12(out_36), .out_13(out_37),
    .out_14(out_38));
  _4_bit_sum u_4_bit_sum_2 (
    .in_1(in_9), .in_2(in_10), .in_3(in_11), .in_4(in_12), .in_5(in_13), .in_6(in_15), .in_7(in_16),
    .in_8(in_18), .out_10(n4_bit_sum_2_out_10), .in_9(n4_bit_sum_3_out_10), .out_11(out_39), .out_12(out_40),
    .out_13(out_41), .out_14(out_42));
  _4_bit_sum u_4_bit_sum_3 (
    .in_1(in_14), .in_2(in_17), .in_3(in_19), .in_4(in_20), .in_5(in_21), .in_6(in_23), .in_7(in_24),
    .in_8(in_26), .out_10(n4_bit_sum_3_out_10), .in_9(n4_bit_sum_4_out_10), .out_11(out_43), .out_12(out_44),
    .out_13(out_45), .out_14(out_46));
  _4_bit_sum u_4_bit_sum_4 (
    .in_1(in_22), .in_2(in_25), .in_3(in_27), .in_4(in_28), .in_5(in_29), .in_6(in_30), .in_7(in_31),
    .in_8(in_32), .out_10(n4_bit_sum_4_out_10), .in_9(in_33), .out_11(out_47), .out_12(out_48),
    .out_13(out_49), .out_14(out_50));
endmodule

module _4_bit_to_base10 (
  input  [3:0] in_1,
  output [9:0] out_2
);

  wire not_1_out, not_2_out, not_3_out, not_4_out, not_5_out, not_6_out, not_7_out, not_8_out, not_9_out,
       not_10_out, not_11_out, not_12_out, not_13_out, not_14_out, not_15_out, not_16_out, not_17_out,
       not_18_out, not_19_out, not_20_out, not_21_out, not_22_out, not_23_out, not_24_out, not_25_out;

  not not_1 (not_1_out, in_1[0]);
  not not_2 (not_2_out, in_1[1]);
  not not_3 (not_3_out, in_1[2]);
  not not_4 (not_4_out, in_1[3]);
  not not_5 (not_5_out, in_1[1]);
  not not_6 (not_6_out, in_1[2]);
  not not_7 (not_7_out, in_1[3]);
  not not_8 (not_8_out, in_1[0]);
  not not_9 (not_9_out, in_1[2]);
  not not_10 (not_10_out, in_1[3]);
  not not_11 (not_11_out, in_1[2]);
  not not_12 (not_12_out, in_1[3]);
  not not_13 (not_13_out, in_1[0]);
  not not_14 (not_14_out, in_1[1]);
  not not_15 (not_15_out, in_1[3]);
  not not_16 (not_16_out, in_1[1]);
  not not_17 (not_17_out, in_1[3]);
  not not_18 (not_18_out, in_1[0]);
  not not_19 (not_19_out, in_1[3]);
  not not_20 (not_20_out, in_1[3]);
  not not_21 (not_21_out, in_1[0]);
  not not_22 (not_22_out, in_1[1]);
  not not_23 (not_23_out, in_1[2]);
  not not_24 (not_24_out, in_1[1]);
  not not_25 (not_25_out, in_1[2]);
  and and_1 (out_2[0], not_1_out, not_2_out, not_3_out, not_4_out);
  and and_2 (out_2[1], in_1[0], not_5_out, not_6_out, not_7_out);
  and and_3 (out_2[2], not_8_out, in_1[1], not_9_out, not_10_out);
  and and_4 (out_2[3], in_1[0], in_1[1], not_11_out, not_12_out);
  and and_5 (out_2[4], not_13_out, not_14_out, in_1[2], not_15_out);
  and and_6 (out_2[5], in_1[0], not_16_out, in_1[2], not_17_out);
  and and_7 (out_2[6], not_18_out, in_1[1], in_1[2], not_19_out);
  and and_8 (out_2[7], in_1[0], in_1[1], in_1[2], not_20_out);
  and and_9 (out_2[8], not_21_out, not_22_out, not_23_out, in_1[3]);
  and and_10 (out_2[9], in_1[0], not_24_out, not_25_out, in_1[3]);
endmodule

module base10_to_display (
  input  [9:0] in_1,
  output [6:0] out_2
);

  or or_1 (out_2[0], in_1[0], in_1[1], in_1[2], in_1[3], in_1[4], in_1[7], in_1[8], in_1[9]);
  or or_2 (out_2[2], in_1[0], in_1[4], in_1[5], in_1[6], in_1[8], in_1[9]);
  or or_3 (out_2[1], in_1[0], in_1[2], in_1[3], in_1[5], in_1[6], in_1[7], in_1[8], in_1[9]);
  or or_4 (out_2[3], in_1[3], in_1[4], in_1[5], in_1[2], in_1[6], in_1[8], in_1[9]);
  or or_5 (out_2[4], in_1[0], in_1[2], in_1[6], in_1[8]);
  or or_6 (out_2[5], in_1[0], in_1[2], in_1[3], in_1[5], in_1[6], in_1[8], in_1[9]);
  or or_7 (out_2[6], in_1[0], in_1[1], in_1[3], in_1[4], in_1[5], in_1[6], in_1[7], in_1[8], in_1[9]);
  _7_Segment_Display u_7_segment_display_1 (
    .g(out_2[3]), .f(out_2[2]), .a(out_2[1]), .b(out_2[0]), .e(out_2[4]), .d(out_2[5]), .c(out_2[6]));  // open: dp
endmodule

module bit_storage (
  input  store,
  input  reset,
  output out_3
);

  wire not_1_out, not_2_out, or_2_out;

  not not_1 (not_1_out, or_2_out);
  not not_2 (not_2_out, out_3);
  or or_1 (out_3, not_1_out, store);
  or or_2 (or_2_out, not_2_out, reset);
endmodule
